# Fritzing sketch SR contr Schematic (saved by Fritzing 1.0.0rc)
breadboards: 1

parts:
  A1 = Particle - Photon2
  U1 = ENCODER_RGB [package=encoder_led_2]
  S1 = Pushbutton [package="[THT]"]
  S2 = Pushbutton [package="[THT]"]
  R1 = Resistor [tolerance=±5% resistance=10000 package="2512 [SMD]"]
  R2 = Resistor [tolerance=±5% resistance=10000 package="2512 [SMD]"]
  Mod1 = Passive Buzzer
  Neopixel1 = Adafruit RBG Smart Neopixel [package="DIP (Dual Inline) [THT]"]
  Neopixel2 = Adafruit RBG Smart Neopixel [package="DIP (Dual Inline) [THT]"]
  OLED_I2C1 = OLED 128x64 I2C Monochrome Display
  M1 = BMP280

nets:
  N1: A1.Pin_17, A1.Pin_18, OLED_I2C1.SDA, OLED_I2C1.SCK, M1.SCL, M1.SDA
  GND: U1.C, R1.Pin_1, R2.Pin_1, Mod1.-, Neopixel1.G, Neopixel2.G, OLED_I2C1.GND, M1.GND
  VDD: U1.+, S1.Pin_3, S1.Pin_4, S2.Pin_3, Mod1.NC, Neopixel1.+, Neopixel2.+, OLED_I2C1.VDD, M1.VIN
  N2: S1.Pin_1, S1.Pin_2, R2.Pin_0
  N3: S2.Pin_1, S2.Pin_2, R1.Pin_0
  N4: Neopixel1.In, Neopixel2.O

custom parts:
  Particle - Photon2: The Photon 2 is a microcontroller and Wi-Fi networking developed by particle. Features: 802.11a/b/g/n Wi-Fi, 2.4 GHz and 5 GHz Integrated PCB antenna Integrated U.FL connector for external antenna Integrated RF switch BLE 5 using same antenna as Wi-Fi Realtek RTL8721DM MCU ARM Cortex M33 CPU, 200 MHz 2048 KB (2 MB) user application maximum size 3072 KB (3 MB) of RAM available to user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
  ENCODER_RGB: SparkFun RGB rotary Encoder
  Pushbutton: A generic pushbutton.
  BMP280: Temperature Humidity Barometric presure Sensor, I2C
